# Fritzing sketch led_rgb_module (saved by Fritzing 0.9.3b)

parts:
  LED1 = RGB LED (com. anode, rbg) [package="5 mm [THT]"]
  U1 = NodeMCU V3.0

nets:
  N1: LED1.red_cathode, U1.3V3
  N2: LED1.common_anode, U1.D1
  N3: LED1.blue_cathode, U1.D3
  N4: LED1.green_cathode, U1.D2

notes:
  RBG module pins
  V, R, B, G

custom parts:
  NodeMCU V3.0: ESP8266 based NodeMCU
