# Fritzing sketch microphone_sensor_test (saved by Fritzing 0.9.3b)

parts:
  U1 = NodeMCU V3.0
  Part1 = Breakout Board for Electret Microphone

nets:
  GND: U1.GND, Part1.GND
  N1: U1.VU, Part1.AUD
  N2: U1.A0, Part1.VCC

notes:
  Pins:
  A0, G, +

custom parts:
  NodeMCU V3.0: ESP8266 based NodeMCU
