# Fritzing sketch soil_moisture_sensor (saved by Fritzing 0.9.3b)

parts:
  Part1 = Soil Moisture Sensor
  U1 = NodeMCU V3.0

nets:
  N1: Part1.SIG, U1.A0
  GND: Part1.GND, U1.GND
  VCC: Part1.VCC, U1.3V3

notes:
  Pins:
  VCC, GND, A0 (SIG)

custom parts:
  NodeMCU V3.0: ESP8266 based NodeMCU
