# Fritzing sketch ultrasonic_web_test (saved by Fritzing 0.9.3b)
breadboards: 1

parts:
  U1 = NodeMCU V3.0
  hc-sr1 = hc-sr04

nets:
  N1: U1.D3, hc-sr1.Trig
  N2: U1.D4, hc-sr1.Echo
  GND: U1.GND, hc-sr1.GND
  N3: U1.VU, hc-sr1.VCC

custom parts:
  NodeMCU V3.0: ESP8266 based NodeMCU
